# Fritzing sketch mtg-scan (saved by Fritzing 0.9.3b)
breadboards: 1

parts:
  SLAVE = Arduino Uno (Rev3)
  MASTER = Arduino Uno (Rev3)
  VCC1 = Battery  # not connected
  J1 = Basic Servo  # not connected
  M1 = DC Motor  # not connected
  LED1 = LED - 5mm [color="Green (555nm)" package="5 mm [THT]"]  # not connected
  LED2 = LED - 5mm [color="Yellow (595nm)" package="5 mm [THT]"]  # not connected
  R1 = Resistor [tolerance=±5% resistance=3.30k package=THT]  # not connected
  R2 = Resistor [tolerance=±5% resistance=3.30k package=THT]  # not connected
  S1 = Pushbutton [package="[THT]"]  # not connected
  S2 = Toggle Switch [package=THT]  # not connected
  S3 = Pushbutton [package="[THT]"]  # not connected
  S4 = Pushbutton [package="[THT]"]  # not connected
  S5 = Pushbutton [package="[THT]"]  # not connected
  S6 = Toggle Switch [package=THT]  # not connected

nets:
  N1: SLAVE.A4/SDA, MASTER.A4/SDA
  N2: SLAVE.A5/SCL, MASTER.A5/SCL

// code stored in the sketch: lcd.ino

// include the library code:


#include <ShiftedLCD.h>

#include <SPI.h>



// initialize the library with the number of the sspin 

// (or the latch pin of the 74HC595)

LiquidCrystal lcd(8);



void setup() {

  // set up the LCD's number of columns and rows: 

  lcd.begin(16, 2);

  // Print a message to the LCD.

  lcd.print("hello, world!");

}



void loop() {

  // set the cursor to column 0, line 1

  // (note: line 1 is the second row, since counting begins with 0):

  lcd.setCursor(0, 1);

  // print the number of seconds since reset:

  lcd.print(millis()/1000);

}


// code stored in the sketch: master.ino
#include <Wire.h>
#include <BreezyArduCAM.h>
#include <ShiftedLCD.h>
#include <SPI.h>

// CAMERA
const int CS_CAM = 10;
// LCD
const int CS_LCD = 2;

// BUTTONS
const int BUTTON_A = 7;
const int BUTTON_B = 6;
const int BUTTON_C = 5;
const int BUTTON_D = 4;
const int SWITCH = 3;

// LEDS
const int LED_GREEN = 9;
const int LED_YELLOW = 8;

// CONST
const int SEND_CARD = 1;
const int OPEN_SERVO = 2;

// SERIAL
const long SERIAL_SPEED = 921600; //921600
const int ARDUINO_ADDRESS = 8;
const int SLAVE_ADDRESS = 8;

// CARD COLORS
const char CARD_NONE = 'N';
const char CARD_UNKNOWN = 'X';
const char CARD_RED = 'R';
const char CARD_GREEN = 'G';
const char CARD_BLUE = 'U';
const char CARD_BLACK = 'B';
const char CARD_WHITE = 'W';
const char CARD_COLORLESS = 'C';
const char CARD_OTHER = 'O';


Serial_ArduCAM_FrameGrabber fg;
ArduCAM_Mini_2MP cardCam(CS_CAM, &fg);

//LiquidCrystal lcd(CS_LCD);

void setup(void)
{
  Wire.begin();
  SPI.begin();

  Serial.begin(SERIAL_SPEED);
  //digitalWrite(CS_CAM, HIGH);
  //digitalWrite(CS_LCD, HIGH);
  cardCam.beginJpeg800x600();

  pinMode(BUTTON_A, INPUT_PULLUP);
  pinMode(BUTTON_B, INPUT_PULLUP);
  pinMode(BUTTON_C, INPUT_PULLUP);
  pinMode(BUTTON_D, INPUT_PULLUP);
  pinMode(SWITCH, INPUT_PULLUP);

  pinMode(LED_GREEN, OUTPUT);
  pinMode(LED_YELLOW, OUTPUT);

  //selectLcd();
  //lcd.begin(16, 2);
  //printLcd("Ready to start!");
}

enum states {
  None,
  Motor1,
  Motor2,
  Waiting,
  Capture
};
states state = Motor1;

void sendToSlave(byte value)
{
  Wire.beginTransmission(SLAVE_ADDRESS);
  Wire.write(value);
  Wire.endTransmission();
}
unsigned long startcaptureTime;

bool modeAuto = false;
void loop(void)
{
  buttonA();
  buttonB();
  buttonC();
  buttonD();

  if (digitalRead(SWITCH) == HIGH) {
    modeAuto = false;
    state = Motor1;
    digitalWrite(LED_GREEN, LOW);
    //selectLcd();
    //lcd.setCursor(0, 0);
    //lcd.print("Mode: manual");
  } else {
    modeAuto = true;
    digitalWrite(LED_GREEN, HIGH);
    //selectLcd();
    //lcd.setCursor(0, 0);
    //lcd.print("Mode: auto  ");
  }

  if (modeAuto) {
    switch (state) {
      case Motor1:
        {
          //printLcd("Sending card");
          sendToSlave(SEND_CARD);
          delay(1000);
          state = Capture;
        }
        break;
      case Capture:
        {
          //printLcd("Capturing image");
          digitalWrite(LED_YELLOW, HIGH);
          cardCam.singleCapture();
          digitalWrite(LED_YELLOW, LOW);
          state = Waiting;
        }
        break;
      case Waiting:
        {
          //printLcd("Waiting data");
          state = Motor2;
          //if (Serial.available()) {
          //  char color = Serial.read();
          //  if (color == 'G') {
          //    state = Motor2;
          //  } else {
          //    state = Motor1;
          //  }
          //}
        }
        break;
      case Motor2:
        {
          //printLcd("Sorting card");
          sendToSlave(OPEN_SERVO);
          state = Motor1;
          delay(500);
        }
        break;
    }
  }
}

void selectCam(void)
{
  //digitalWrite(CS_CAM, LOW);
  //digitalWrite(CS_LCD, HIGH);
}

void selectLcd(void)
{
  //digitalWrite(CS_CAM, HIGH);
  //digitalWrite(CS_LCD, LOW);
}

void printLcd(char message[])
{
  //selectLcd();
  //lcd.setCursor(0, 1);
  //lcd.print(message);
  //digitalWrite(CS_LCD, HIGH);
}

// SEND CARD
void buttonA()
{
  if (digitalRead(BUTTON_A) == LOW) {
    sendToSlave(SEND_CARD);
  }
}

// SEND CARD TO SORTING
void buttonB()
{
  if (digitalRead(BUTTON_B) == LOW) {
    sendToSlave(OPEN_SERVO);
  }
}

// TAKE CAMERA PICTURE
bool capturing = false;
void buttonC(void) {
  if (!capturing && digitalRead(BUTTON_C) == LOW) {
    //printLcd("Manual capture..");
    //selectCam();
    capturing = true;
    digitalWrite(LED_YELLOW, HIGH);
    cardCam.singleCapture();
    digitalWrite(LED_YELLOW, LOW);
    capturing = false;
    //printLcd("                ");
  }
}

void buttonD(void) {
}

// code stored in the sketch: slave.ino
#include <Servo.h>
#include <Wire.h>

Servo cardServo;

// MOTORS
const int MOTOR_CARD_FORWARD = 9;
const int MOTOR_CARD_BACKWARD = 10;
const int MOTOR_CARD_PWM = 11;
const int MOTOR_CARD_FORWARD_TIME = 650; //ms
const int MOTOR_CARD_BACKWARD_TIME = 130; //ms
const int SERVO_CARD = 2;
const int SERVO_CLOSE = 60;
const int SERVO_OPEN = 130;
const int SERVO_OPEN_TIME = 250; //ms

// SERIAL
const long SERIAL_SPEED = 921600; //921600
const int ARDUINO_ADDRESS = 8;

// CARD COLORS
const int CARD_NONE = 0;
const int CARD_UNKNOWN = -1;
const int CARD_RED = 1;
const int CARD_GREEN = 2;
const int CARD_BLUE = 3;
const int CARD_BLACK = 4;
const int CARD_WHITE = 5;
const int CARD_COLORLESS = 6;
const int CARD_OTHER = 7;

void setup(void)
{
  Serial.begin(SERIAL_SPEED);

  pinMode(MOTOR_CARD_FORWARD, OUTPUT);
  pinMode(MOTOR_CARD_BACKWARD, OUTPUT);
  pinMode(MOTOR_CARD_PWM, OUTPUT);
  pinMode(SERVO_CARD, OUTPUT);

  cardServo.attach(SERVO_CARD);
  cardServo.write(SERVO_CLOSE);

  Wire.begin(ARDUINO_ADDRESS);
  Wire.onReceive(receiveEvent);
}

bool send_card = false;
bool sort_card = false;
void receiveEvent(int howMany) {
  int x = Wire.read();
  if (x == 1) {
    send_card = true;
  } else if (x == 2) {
    sort_card = true;
  }
}

bool serving_new_card = false;
bool prepare_new_card = false;
unsigned long serving_card_start = 0;
void sendCardtoAnalyse(void)
{
  if (!serving_new_card && !prepare_new_card && send_card) {
    serving_new_card = true;
    serving_card_start = millis();
    analogWrite(MOTOR_CARD_FORWARD, 255);
    analogWrite(MOTOR_CARD_BACKWARD, 0);
    analogWrite(MOTOR_CARD_PWM, 90);
  }

  if (serving_new_card && (millis() - serving_card_start) > MOTOR_CARD_FORWARD_TIME) {
    serving_new_card = false;
    prepare_new_card = true;
    analogWrite(MOTOR_CARD_FORWARD, 0);
    analogWrite(MOTOR_CARD_BACKWARD, 255);
    analogWrite(MOTOR_CARD_PWM, 255);
  }

  if (prepare_new_card && (millis() - serving_card_start) > MOTOR_CARD_FORWARD_TIME + MOTOR_CARD_BACKWARD_TIME) {
    send_card = false;
    prepare_new_card = false;
    analogWrite(MOTOR_CARD_FORWARD, 0);
    analogWrite(MOTOR_CARD_BACKWARD, 0);
  }
}

bool sorting_card = false;
unsigned long sorting_card_start = 0;
void sendCardToSorting()
{
  if (!sorting_card && sort_card) {
    sorting_card = true;
    sort_card = false;
    sorting_card_start = millis();
    cardServo.write(SERVO_OPEN);
  }

  if (sorting_card && (millis() - sorting_card_start) > SERVO_OPEN_TIME) {
    sorting_card = false;
    cardServo.write(SERVO_CLOSE);
  }
}

void loop(void)
{
  sendCardtoAnalyse();
  sendCardToSorting();
}
